// Logisim project CPU.circ as structural Verilog: 15 circuits, main circuit Processor
module Processor (
  input  in_1
);

  wire and_1_out, and_2_out, and_3_out, and_4_out, binarytobcd_1_sup_out, binarytobcd_2_sup_out,
       binarytobcd_3_sup_out, binarytobcd_4_sup_out, binarytobcd_5_sup_out, binarytobcd_6_sup_out,
       binarytobcd_7_sup_out, binarytobcd_8_sup_out, binarytobcd_9_sup_out, businterface_1_bm0,
       businterface_1_bm1, businterface_1_bm2, businterface_1_bm3, businterface_1_nrw, businterface_1_strobe,
       button_1_out, button_2_out, CLK, clock_1_out, comparator_1_eq, comparator_2_eq, comparator_3_eq,
       controlstatusregisters_1_eie, controlstatusregisters_1_ill, EAL, EPL, EQ, fetchunit_1_ldsx,
       fetchunit_1_load0, fetchunit_1_load1, fetchunit_1_pce, fetchunit_1_store0, fetchunit_1_store1,
       instructiondecoder_1_brk, instructiondecoder_1_csr_bit, instructiondecoder_1_csr_clr,
       instructiondecoder_1_csr_en, instructiondecoder_1_hold, instructiondecoder_1_ill,
       instructiondecoder_1_ld0, instructiondecoder_1_ld1, instructiondecoder_1_ret,
       instructiondecoder_1_st0, instructiondecoder_1_st1, instructiondecoder_1_sx, instructiondecoder_1_sys,
       instructiondecoder_1_wfi, interruptcontroller_1_rdy, interruptcontroller_1_trap, IRG, IRQ, JMP, LCS,
       LDR, LNK, LT, LTU, not_1_out, not_2_out, OPI, RDY, REL, RST, SET;
  wire [4:0] RD, RS1, RS2, SEL;
  wire [11:0] instructiondecoder_1_csri;
  wire [13:0] businterface_1_a_2;
  wire [15:0] businterface_1_a, register_1_q, register_2_q;
  wire [31:0] ALU, binarytobcd_2_vout, binarytobcd_3_vout, binarytobcd_4_vout, binarytobcd_5_vout,
       binarytobcd_6_vout, binarytobcd_7_vout, binarytobcd_8_vout, binarytobcd_9_vout, binarytobcd_10_vout,
       bit_extender_1_out, bit_extender_2_out, controlstatusregisters_1_epc, controlstatusregisters_1_isr,
       CSR, fetchunit_1_addr, fetchunit_1_instr, IMM, interruptcontroller_1_cause, MDI, NPC, PC, ram_1_data,
       REF, register_3_q, RES, rom_1_data, RX, RY, shifter_1_out, shifter_2_out;

  not not_1 (not_1_out, not_2_out);
  assign bit_extender_1_out = {{2{businterface_1_a_2[13]}}, {businterface_1_a_2, businterface_1_a}};  // Bit_Extender bit_extender_1
  _7_Segment_Display u_7_segment_display_1 ();  // open: g, f, a, b, e, d, c, dp
  _7_Segment_Display u_7_segment_display_2 ();  // open: g, f, a, b, e, d, c, dp
  // BCD_to_7_Segment_decoder bcd_to_7_segment_decoder_1: pin names not known
  // BCD_to_7_Segment_decoder bcd_to_7_segment_decoder_2: pin names not known
  BinaryToBCD binarytobcd_1 (
    .SUP_OUT(binarytobcd_1_sup_out), .VIN(binarytobcd_2_vout), .SUP_IN(1'b1), .SUP_0(1'b1));  // open: VOUT, DIGIT
  BinaryToBCD binarytobcd_2 (
    .VOUT(binarytobcd_2_vout), .SUP_OUT(binarytobcd_2_sup_out), .VIN(binarytobcd_3_vout),
    .SUP_IN(binarytobcd_1_sup_out), .SUP_0(1'b1));  // open: DIGIT
  Comparator #(.width(14)) comparator_1 (.a(businterface_1_a_2), .b({14{1'b1}}), .eq(comparator_1_eq));  // open: gt, lt
  Comparator #(.width(14)) comparator_2 (.a(businterface_1_a_2), .b(14'h200), .eq(comparator_2_eq));  // open: gt, lt
  and and_1 (and_1_out, not_1_out, comparator_2_eq);
  and and_2 (and_2_out, comparator_2_eq, not_2_out);
  Shifter #(.width(32)) shifter_1 (.in(bit_extender_1_out), .\dist (5'b00010), .out(shifter_1_out));
  _7_Segment_Display u_7_segment_display_3 ();  // open: g, f, a, b, e, d, c, dp
  // BCD_to_7_Segment_decoder bcd_to_7_segment_decoder_3: pin names not known
  BinaryToBCD binarytobcd_3 (
    .VOUT(binarytobcd_3_vout), .SUP_OUT(binarytobcd_3_sup_out), .VIN(binarytobcd_4_vout),
    .SUP_IN(binarytobcd_2_sup_out), .SUP_0(1'b1));  // open: DIGIT
  ROM #(.addrWidth(16), .dataWidth(32)) rom_1 (.addr(register_1_q), .data(rom_1_data));
  Register #(.trigger("high"), .width(16)) register_1 (
    .D(businterface_1_a), .Q(register_1_q), .clk(comparator_1_eq));  // open: en, clr
  RAM #(.addrWidth(16), .asyncread("true"), .byteenables("byteEnables"), .dataWidth(32), .databus("bidir"), .trigger("falling")) ram_1 (
    .addr(register_2_q), .we(and_1_out), .oe(and_2_out), .clk(businterface_1_strobe), .data(ram_1_data),
    .be3(businterface_1_bm3), .be2(businterface_1_bm2), .be1(businterface_1_bm1), .be0(businterface_1_bm0));
  Register #(.trigger("high"), .width(16)) register_2 (
    .D(businterface_1_a), .Q(register_2_q), .clk(comparator_2_eq));  // open: en, clr
  and and_3 (and_3_out, ~not_2_out, comparator_3_eq);  // AND_Gate
  Comparator #(.width(32)) comparator_3 (.a(shifter_1_out), .b(32'hc0008000), .eq(comparator_3_eq));  // open: gt, lt
  _7_Segment_Display u_7_segment_display_4 ();  // open: g, f, a, b, e, d, c, dp
  _7_Segment_Display u_7_segment_display_5 ();  // open: g, f, a, b, e, d, c, dp
  // BCD_to_7_Segment_decoder bcd_to_7_segment_decoder_4: pin names not known
  // BCD_to_7_Segment_decoder bcd_to_7_segment_decoder_5: pin names not known
  BinaryToBCD binarytobcd_4 (
    .VOUT(binarytobcd_4_vout), .SUP_OUT(binarytobcd_4_sup_out), .VIN(binarytobcd_5_vout),
    .SUP_IN(binarytobcd_3_sup_out), .SUP_0(1'b1));  // open: DIGIT
  BinaryToBCD binarytobcd_5 (
    .VOUT(binarytobcd_5_vout), .SUP_OUT(binarytobcd_5_sup_out), .VIN(binarytobcd_6_vout),
    .SUP_IN(binarytobcd_4_sup_out), .SUP_0(1'b1));  // open: DIGIT
  Register #(.width(32)) register_3 (
    .D(ram_1_data), .en(and_3_out), .clk(businterface_1_strobe), .Q(register_3_q));  // open: clr
  _7_Segment_Display u_7_segment_display_6 ();  // open: g, f, a, b, e, d, c, dp
  _7_Segment_Display u_7_segment_display_7 ();  // open: g, f, a, b, e, d, c, dp
  // BCD_to_7_Segment_decoder bcd_to_7_segment_decoder_6: pin names not known
  // BCD_to_7_Segment_decoder bcd_to_7_segment_decoder_7: pin names not known
  BinaryToBCD binarytobcd_6 (
    .VOUT(binarytobcd_6_vout), .SUP_OUT(binarytobcd_6_sup_out), .VIN(binarytobcd_7_vout),
    .SUP_IN(binarytobcd_5_sup_out), .SUP_0(1'b1));  // open: DIGIT
  _7_Segment_Display u_7_segment_display_8 ();  // open: g, f, a, b, e, d, c, dp
  // BCD_to_7_Segment_decoder bcd_to_7_segment_decoder_8: pin names not known
  BinaryToBCD binarytobcd_7 (
    .VOUT(binarytobcd_7_vout), .SUP_OUT(binarytobcd_7_sup_out), .VIN(binarytobcd_8_vout),
    .SUP_IN(binarytobcd_6_sup_out), .SUP_0(1'b1));  // open: DIGIT
  BinaryToBCD binarytobcd_8 (
    .VOUT(binarytobcd_8_vout), .SUP_OUT(binarytobcd_8_sup_out), .VIN(binarytobcd_9_vout),
    .SUP_IN(binarytobcd_7_sup_out), .SUP_0(1'b1));  // open: DIGIT
  assign bit_extender_2_out = {{2{businterface_1_a_2[13]}}, {businterface_1_a_2, businterface_1_a}};  // Bit_Extender bit_extender_2
  assign ram_1_data = and_4_out ? rom_1_data : 32'bz;  // Controlled_Buffer controlled_buffer_1
  and and_4 (and_4_out, comparator_1_eq, not_2_out);
  _7_Segment_Display u_7_segment_display_9 ();  // open: g, f, a, b, e, d, c, dp
  _7_Segment_Display u_7_segment_display_10 ();  // open: g, f, a, b, e, d, c, dp
  // BCD_to_7_Segment_decoder bcd_to_7_segment_decoder_9: pin names not known
  // BCD_to_7_Segment_decoder bcd_to_7_segment_decoder_10: pin names not known
  BinaryToBCD binarytobcd_9 (
    .VOUT(binarytobcd_9_vout), .SUP_OUT(binarytobcd_9_sup_out), .VIN(binarytobcd_10_vout),
    .SUP_IN(binarytobcd_8_sup_out), .SUP_0(1'b1));  // open: DIGIT
  BinaryToBCD binarytobcd_10 (
    .VOUT(binarytobcd_10_vout), .VIN(register_3_q), .SUP_IN(binarytobcd_9_sup_out), .SUP_0(1'b0));  // open: SUP_OUT, DIGIT
  // Probe on shifter_2_out
  Shifter #(.width(32)) shifter_2 (.in(bit_extender_2_out), .\dist (5'b00010), .out(shifter_2_out));
  // Probe on ram_1_data
  BusInterface businterface_1 (
    .DIN(MDI), .A({businterface_1_a_2, businterface_1_a}), .STROBE(businterface_1_strobe), .EALIGN(EAL),
    .BM0(businterface_1_bm0), .BM1(businterface_1_bm1), .BM2(businterface_1_bm2), .BM3(businterface_1_bm3),
    .nRW(businterface_1_nrw), .DO(ram_1_data), .DI(ram_1_data), .DOUT(RY), .RST(RST), .CLK(CLK),
    .LDSX(fetchunit_1_ldsx), .LOAD0(fetchunit_1_load0), .LOAD1(fetchunit_1_load1),
    .STORE0(fetchunit_1_store0), .STORE1(fetchunit_1_store1), .ADDR(fetchunit_1_addr));
  not not_2 (not_2_out, businterface_1_nrw);
  RegisterFile registerfile_1 (.Y(RY), .X(RX), .YI(RS2), .D(RES), .CLK(CLK), .WI(RD), .XI(RS1));
  FetchUnit fetchunit_1 (
    .INSTR(fetchunit_1_instr), .ADDR(fetchunit_1_addr), .PC(PC), .PCE(fetchunit_1_pce),
    .LDSX(fetchunit_1_ldsx), .LOAD0(fetchunit_1_load0), .LOAD(LDR), .LOAD1(fetchunit_1_load1),
    .STORE0(fetchunit_1_store0), .STORE1(fetchunit_1_store1), .GRANT(IRG), .EMA(ALU), .PC_IN(NPC), .CLK(CLK),
    .IRQ(IRQ), .HOLD(instructiondecoder_1_hold), .SX(instructiondecoder_1_sx),
    .LD0(instructiondecoder_1_ld0), .LD1(instructiondecoder_1_ld1), .ST0(instructiondecoder_1_st0),
    .ST1(instructiondecoder_1_st1), .DIN(MDI));
  ProgramCounter programcounter_1 (.EALIGN(EPL), .PC(NPC), .PCE(fetchunit_1_pce), .CLK(CLK), .JMP(SET), .ADDR(REF));
  InstructionDecoder instructiondecoder_1 (
    .RS1(RS1), .ST0(instructiondecoder_1_st0), .ST1(instructiondecoder_1_st1),
    .CSR_BIT(instructiondecoder_1_csr_bit), .CSR_CLR(instructiondecoder_1_csr_clr), .ALU_OP(SEL),
    .PCREL(REL), .OPIMM(OPI), .BRANCH(JMP), .LINK(LNK), .SX(instructiondecoder_1_sx),
    .LD0(instructiondecoder_1_ld0), .LD1(instructiondecoder_1_ld1), .CSR_EN(instructiondecoder_1_csr_en),
    .HOLD(instructiondecoder_1_hold), .RS2(RS2), .CSRI(instructiondecoder_1_csri), .IMM(IMM),
    .WFI(instructiondecoder_1_wfi), .SYS(instructiondecoder_1_sys), .RET(instructiondecoder_1_ret),
    .BRK(instructiondecoder_1_brk), .ILL(instructiondecoder_1_ill), .RD(RD),
    .READY(interruptcontroller_1_rdy), .CLK(CLK), .RST(RST), .EQ(EQ), .LT(LT), .LTU(LTU),
    .INSTR(fetchunit_1_instr));
  ResultMux resultmux_1 (.RES(RES), .ALU(ALU), .NPC(NPC), .MDI(MDI), .CSR(CSR), .LINK(LNK), .LOAD(LDR), .LDCSR(LCS));
  Clock clock_1 (.out(clock_1_out));
  xor xor_1 (CLK, clock_1_out, button_1_out);
  Button button_1 (.out(button_1_out));
  not not_3 (RST, in_1);
  InterruptController interruptcontroller_1 (
    .RDY(interruptcontroller_1_rdy), .IRQ(IRQ), .CAUSE(interruptcontroller_1_cause), .REF(REF), .SET(SET),
    .TRAP(interruptcontroller_1_trap), .GRANT(IRG), .CLK(CLK), .ALU(ALU), .EPC(controlstatusregisters_1_epc),
    .ISR(controlstatusregisters_1_isr), .TRIG(button_2_out), .EIE(controlstatusregisters_1_eie), .JMP(JMP),
    .RET(instructiondecoder_1_ret), .RST(RST), .RDY_IN(RDY), .WFI(instructiondecoder_1_wfi), .LDR(LDR),
    .EAL(EAL), .EPL(EPL), .ILL(controlstatusregisters_1_ill), .SYS(instructiondecoder_1_sys),
    .BRK(instructiondecoder_1_brk));
  Button button_2 (.out(button_2_out));
  ArithmeticLogicUnit arithmeticlogicunit_1 (
    .R(ALU), .RDY(RDY), .EQ(EQ), .LT(LT), .LTU(LTU), .SEL(SEL), .A(RX), .PC(PC), .PCREL(REL), .B(RY),
    .IMM(IMM), .OPIMM(OPI), .CLK(CLK));
  ControlStatusRegisters controlstatusregisters_1 (
    .ISR(controlstatusregisters_1_isr), .ILL(controlstatusregisters_1_ill),
    .EPC(controlstatusregisters_1_epc), .CSR_OUT(CSR), .EIE(controlstatusregisters_1_eie), .LDCSR(LCS),
    .RST(RST), .ILL_IN(instructiondecoder_1_ill), .CLR(instructiondecoder_1_csr_clr),
    .IRET(instructiondecoder_1_ret), .OPIMM(OPI), .CSR(instructiondecoder_1_csri), .RX(RX), .IMM(IMM),
    .BIT(instructiondecoder_1_csr_bit), .CSE(instructiondecoder_1_csr_en), .PC(PC),
    .CAUSE_IN(interruptcontroller_1_cause), .TRAP(interruptcontroller_1_trap), .CLK(CLK));

  // Notes on the sheet:
  //   contents of rom_1 (hex, n*v repeats v):
  //   f8010113 112223 212423 312623 412823 512a23 612c23 712e23 2812023 2912223 2a12423 2b12623 2c12823
  //   2d12a23 2e12c23 2f12e23 5012023 5112223 5212423 5312623 5412823 5512a23 5612c23 5712e23 7812023
  //   7912223 7a12423 7b12623 7c12823 7d12a23 7e12c23 7f12e23 341022f3 512023 10513 342025f3 cc000ef 12283
  //   34129073 7c12f83 7812f03 7412e83 7012e03 6c12d83 6812d03 6412c83 6012c03 5c12b83 5812b03 5412a83
  //   5012a03 4c12983 4812903 4412883 4012803 3c12783 3812703 3412683 3012603 2c12583 2812503 2412483
  //   2012403 1c12383 1812303 1412283 1012203 c12183 812103 412083 8010113 30200073 100513 50593 73 8067
  //   c00087b7 a7a023 8067 2852703 100793 f70463 8067 2c52703 c00087b7 e7a023 8067 b00793 2f58463 800007b7
  //   b78793 f59c63 5f5e7b7 c0008737 ff78793 f72023 8067 8067 2852703 100793 f71863 2c52703 c00087b7
  //   e7a023 52783 478793 f52023 8067 100613 100513 60593 73 100513 60593 73 100713 200793 100513 78593 73
  //   f706b3 e6b5b3 78713 fc0594e3 68793 100513 78593 73 f706b3 e6b5b3 78713 fa0594e3 fe1ff06f 65339*0
  //   8004117 10010113 fffc0297 f828293 30529073 fffc0297 29c28293 34129073 12b7 80028293 3042a073 8000293
  //   3002a073 30200073
endmodule

module RegisterFile (
  input  CLK,
  input  [4:0] WI,
  input  [31:0] D,
  input  [4:0] XI,
  input  [4:0] YI,
  output [31:0] X,
  output [31:0] Y
);

  wire W1, W2, W3, W4, W5, W6, W7, W8, W9, W10, W11, W12, W13, W14, W15, W16, W17, W18, W19, W20, W21, W22,
       W23, W24, W25, W26, W27, W28, W29, W30, W31;
  wire [31:0] decoder_1_out0, decoder_4_out0, L0_p2, R1, R2, R3, R4, R5, R6, R7, R8, R9, R10, R11, R12, R13,
       R14, R15, R16, R17, R18, R19, R20, R21, R22, R23, R24, R25, R26, R27, R28, R29, R30, R31;

  Decoder #(.enable("false"), .select(5)) decoder_1 (
    .out0(decoder_1_out0[0]), .out1(decoder_1_out0[1]), .out2(decoder_1_out0[2]), .out3(decoder_1_out0[3]),
    .out4(decoder_1_out0[4]), .out5(decoder_1_out0[5]), .out6(decoder_1_out0[6]), .out7(decoder_1_out0[7]),
    .out8(decoder_1_out0[8]), .out9(decoder_1_out0[9]), .out10(decoder_1_out0[10]),
    .out11(decoder_1_out0[11]), .out12(decoder_1_out0[12]), .out13(decoder_1_out0[13]),
    .out14(decoder_1_out0[14]), .out15(decoder_1_out0[15]), .out16(decoder_1_out0[16]),
    .out17(decoder_1_out0[17]), .out18(decoder_1_out0[18]), .out19(decoder_1_out0[19]),
    .out20(decoder_1_out0[20]), .out21(decoder_1_out0[21]), .out22(decoder_1_out0[22]),
    .out23(decoder_1_out0[23]), .out24(decoder_1_out0[24]), .out25(decoder_1_out0[25]),
    .out26(decoder_1_out0[26]), .out27(decoder_1_out0[27]), .out28(decoder_1_out0[28]),
    .out29(decoder_1_out0[29]), .out30(decoder_1_out0[30]), .out31(decoder_1_out0[31]), .sel(XI));
  // RGBLED L31: pin names not known; wires that end beside it: decoder_1_out0[31], L0_p2[31]
  // RGBLED L30: pin names not known; wires that end beside it: decoder_1_out0[30], L0_p2[30]
  Register #(.width(32)) register_1 (.D(D), .en(W1), .clk(CLK), .Q(R1));  // open: clr
  Register #(.width(32)) register_2 (.D(D), .en(W2), .clk(CLK), .Q(R2));  // open: clr
  Register #(.width(32)) register_3 (.D(D), .en(W3), .clk(CLK), .Q(R3));  // open: clr
  Register #(.trigger("high"), .width(32)) DATA (.D(D), .clk(1'b1));  // open: en, Q, clr
  // RGBLED L29: pin names not known; wires that end beside it: decoder_1_out0[29], L0_p2[29]
  // RGBLED L28: pin names not known; wires that end beside it: decoder_1_out0[28], L0_p2[28]
  // RGBLED L27: pin names not known; wires that end beside it: decoder_1_out0[27], L0_p2[27]
  // RGBLED L26: pin names not known; wires that end beside it: decoder_1_out0[26], L0_p2[26]
  Register #(.width(32)) register_4 (.D(D), .en(W4), .clk(CLK), .Q(R4));  // open: clr
  Register #(.width(32)) register_5 (.D(D), .en(W5), .clk(CLK), .Q(R5));  // open: clr
  Register #(.width(32)) register_6 (.D(D), .en(W6), .clk(CLK), .Q(R6));  // open: clr
  Register #(.width(32)) register_7 (.D(D), .en(W7), .clk(CLK), .Q(R7));  // open: clr
  // RGBLED L25: pin names not known; wires that end beside it: decoder_1_out0[25], L0_p2[25]
  Decoder #(.enable("false"), .select(5)) decoder_2 (
    .out1(W1), .out2(W2), .out3(W3), .out4(W4), .out5(W5), .out6(W6), .out7(W7), .out8(W8), .out9(W9),
    .out10(W10), .out11(W11), .out12(W12), .out13(W13), .out14(W14), .out15(W15), .out16(W16), .out17(W17),
    .out18(W18), .out19(W19), .out20(W20), .out21(W21), .out22(W22), .out23(W23), .out24(W24), .out25(W25),
    .out26(W26), .out27(W27), .out28(W28), .out29(W29), .out30(W30), .out31(W31), .sel(WI));  // open: out0
  // RGBLED L24: pin names not known; wires that end beside it: decoder_1_out0[24], L0_p2[24]
  // RGBLED L23: pin names not known; wires that end beside it: decoder_1_out0[23], L0_p2[23]
  // RGBLED L22: pin names not known; wires that end beside it: decoder_1_out0[22], L0_p2[22]
  Register #(.width(32)) register_8 (.D(D), .en(W8), .clk(CLK), .Q(R8));  // open: clr
  Register #(.width(32)) register_9 (.D(D), .en(W9), .clk(CLK), .Q(R9));  // open: clr
  Register #(.width(32)) register_10 (.D(D), .en(W10), .clk(CLK), .Q(R10));  // open: clr
  Register #(.width(32)) register_11 (.D(D), .en(W11), .clk(CLK), .Q(R11));  // open: clr
  // RGBLED L21: pin names not known; wires that end beside it: decoder_1_out0[21], L0_p2[21]
  // RGBLED L20: pin names not known; wires that end beside it: decoder_1_out0[20], L0_p2[20]
  // RGBLED L19: pin names not known; wires that end beside it: decoder_1_out0[19], L0_p2[19]
  // RGBLED L18: pin names not known; wires that end beside it: decoder_1_out0[18], L0_p2[18]
  Register #(.width(32)) register_12 (.D(D), .en(W12), .clk(CLK), .Q(R12));  // open: clr
  Register #(.width(32)) register_13 (.D(D), .en(W13), .clk(CLK), .Q(R13));  // open: clr
  Register #(.width(32)) register_14 (.D(D), .en(W14), .clk(CLK), .Q(R14));  // open: clr
  Register #(.width(32)) register_15 (.D(D), .en(W15), .clk(CLK), .Q(R15));  // open: clr
  // RGBLED L17: pin names not known; wires that end beside it: decoder_1_out0[17], L0_p2[17]
  Multiplexer #(.select(5), .width(32)) multiplexer_1 (
    .in0({32{1'b0}}), .in1(R1), .in2(R2), .in3(R3), .in4(R4), .in5(R5), .in6(R6), .in7(R7), .in8(R8),
    .in9(R9), .in10(R10), .in11(R11), .in12(R12), .in13(R13), .in14(R14), .in15(R15), .in16(R16), .in17(R17),
    .in18(R18), .in19(R19), .in20(R20), .in21(R21), .in22(R22), .in23(R23), .in24(R24), .in25(R25),
    .in26(R26), .in27(R27), .in28(R28), .in29(R29), .in30(R30), .in31(R31), .out(X), .sel(XI));
  // RGBLED L16: pin names not known; wires that end beside it: decoder_1_out0[16], L0_p2[16]
  // RGBLED L15: pin names not known; wires that end beside it: decoder_1_out0[15], L0_p2[15]
  Register #(.width(32)) register_16 (.D(D), .en(W16), .clk(CLK), .Q(R16));  // open: clr
  Register #(.width(32)) register_17 (.D(D), .en(W17), .clk(CLK), .Q(R17));  // open: clr
  Register #(.width(32)) register_18 (.D(D), .en(W18), .clk(CLK), .Q(R18));  // open: clr
  Register #(.width(32)) register_19 (.D(D), .en(W19), .clk(CLK), .Q(R19));  // open: clr
  Register #(.trigger("high"), .width(32)) RX (.D(X), .clk(1'b1));  // open: en, Q, clr
  // RGBLED L14: pin names not known; wires that end beside it: decoder_1_out0[14], L0_p2[14]
  // RGBLED L13: pin names not known; wires that end beside it: decoder_1_out0[13], L0_p2[13]
  // RGBLED L12: pin names not known; wires that end beside it: decoder_1_out0[12], L0_p2[12]
  Register #(.width(32)) register_20 (.D(D), .en(W20), .clk(CLK), .Q(R20));  // open: clr
  Register #(.width(32)) register_21 (.D(D), .en(W21), .clk(CLK), .Q(R21));  // open: clr
  Register #(.width(32)) register_22 (.D(D), .en(W22), .clk(CLK), .Q(R22));  // open: clr
  Register #(.width(32)) register_23 (.D(D), .en(W23), .clk(CLK), .Q(R23));  // open: clr
  // RGBLED L11: pin names not known; wires that end beside it: decoder_1_out0[11], L0_p2[11]
  // RGBLED L10: pin names not known; wires that end beside it: decoder_1_out0[10], L0_p2[10]
  // RGBLED L9: pin names not known; wires that end beside it: decoder_1_out0[9], L0_p2[9]
  Register #(.width(32)) register_24 (.D(D), .en(W24), .clk(CLK), .Q(R24));  // open: clr
  Register #(.width(32)) register_25 (.D(D), .en(W25), .clk(CLK), .Q(R25));  // open: clr
  Register #(.width(32)) register_26 (.D(D), .en(W26), .clk(CLK), .Q(R26));  // open: clr
  Register #(.width(32)) register_27 (.D(D), .en(W27), .clk(CLK), .Q(R27));  // open: clr
  // RGBLED L8: pin names not known; wires that end beside it: decoder_1_out0[8], L0_p2[8]
  // RGBLED L7: pin names not known; wires that end beside it: decoder_1_out0[7], L0_p2[7]
  // RGBLED L6: pin names not known; wires that end beside it: decoder_1_out0[6], L0_p2[6]
  Register #(.width(32)) register_28 (.D(D), .en(W28), .clk(CLK), .Q(R28));  // open: clr
  Register #(.width(32)) register_29 (.D(D), .en(W29), .clk(CLK), .Q(R29));  // open: clr
  Register #(.width(32)) register_30 (.D(D), .en(W30), .clk(CLK), .Q(R30));  // open: clr
  Register #(.width(32)) register_31 (.D(D), .en(W31), .clk(CLK), .Q(R31));  // open: clr
  Multiplexer #(.select(5), .width(32)) multiplexer_2 (
    .in0({32{1'b0}}), .in1(R1), .in2(R2), .in3(R3), .in4(R4), .in5(R5), .in6(R6), .in7(R7), .in8(R8),
    .in9(R9), .in10(R10), .in11(R11), .in12(R12), .in13(R13), .in14(R14), .in15(R15), .in16(R16), .in17(R17),
    .in18(R18), .in19(R19), .in20(R20), .in21(R21), .in22(R22), .in23(R23), .in24(R24), .in25(R25),
    .in26(R26), .in27(R27), .in28(R28), .in29(R29), .in30(R30), .in31(R31), .out(Y), .sel(YI));
  // RGBLED L5: pin names not known; wires that end beside it: decoder_1_out0[5], L0_p2[5]
  // RGBLED L4: pin names not known; wires that end beside it: decoder_1_out0[4], L0_p2[4]
  Register #(.trigger("high"), .width(32)) RY (.D(Y), .clk(1'b1));  // open: en, Q, clr
  // RGBLED L3: pin names not known; wires that end beside it: decoder_1_out0[3], L0_p2[3]
  // RGBLED L2: pin names not known; wires that end beside it: decoder_1_out0[2], L0_p2[2]
  // RGBLED L1: pin names not known; wires that end beside it: decoder_1_out0[1], L0_p2[1]
  // RGBLED L0: pin names not known; wires that end beside it: decoder_1_out0[0], L0_p2[0]
  Decoder #(.enable("false"), .select(5)) decoder_3 (
    .out0(L0_p2[0]), .out1(L0_p2[1]), .out2(L0_p2[2]), .out3(L0_p2[3]), .out4(L0_p2[4]), .out5(L0_p2[5]),
    .out6(L0_p2[6]), .out7(L0_p2[7]), .out8(L0_p2[8]), .out9(L0_p2[9]), .out10(L0_p2[10]), .out11(L0_p2[11]),
    .out12(L0_p2[12]), .out13(L0_p2[13]), .out14(L0_p2[14]), .out15(L0_p2[15]), .out16(L0_p2[16]),
    .out17(L0_p2[17]), .out18(L0_p2[18]), .out19(L0_p2[19]), .out20(L0_p2[20]), .out21(L0_p2[21]),
    .out22(L0_p2[22]), .out23(L0_p2[23]), .out24(L0_p2[24]), .out25(L0_p2[25]), .out26(L0_p2[26]),
    .out27(L0_p2[27]), .out28(L0_p2[28]), .out29(L0_p2[29]), .out30(L0_p2[30]), .out31(L0_p2[31]), .sel(YI));
  Decoder #(.enable("false"), .select(5)) decoder_4 (
    .out0(decoder_4_out0[0]), .out1(decoder_4_out0[1]), .out2(decoder_4_out0[2]), .out3(decoder_4_out0[3]),
    .out4(decoder_4_out0[4]), .out5(decoder_4_out0[5]), .out6(decoder_4_out0[6]), .out7(decoder_4_out0[7]),
    .out8(decoder_4_out0[8]), .out9(decoder_4_out0[9]), .out10(decoder_4_out0[10]),
    .out11(decoder_4_out0[11]), .out12(decoder_4_out0[12]), .out13(decoder_4_out0[13]),
    .out14(decoder_4_out0[14]), .out15(decoder_4_out0[15]), .out16(decoder_4_out0[16]),
    .out17(decoder_4_out0[17]), .out18(decoder_4_out0[18]), .out19(decoder_4_out0[19]),
    .out20(decoder_4_out0[20]), .out21(decoder_4_out0[21]), .out22(decoder_4_out0[22]),
    .out23(decoder_4_out0[23]), .out24(decoder_4_out0[24]), .out25(decoder_4_out0[25]),
    .out26(decoder_4_out0[26]), .out27(decoder_4_out0[27]), .out28(decoder_4_out0[28]),
    .out29(decoder_4_out0[29]), .out30(decoder_4_out0[30]), .out31(decoder_4_out0[31]), .sel(WI));

  // Other names for the same wires on the sheet: DI[31:0] = D
endmodule

module ProgramCounter (
  input  PCE,
  input  CLK,
  input  JMP,
  input  [31:0] ADDR,
  output EALIGN,
  output [31:0] PC
);

  wire or_1_out;

  and and_1 (EALIGN, or_1_out, JMP);
  or or_1 (or_1_out, ADDR[0], ADDR[1]);
  Counter #(.max('h3fffffff), .width(30)) counter_1 (
    .load(JMP), .count(PCE), .clk(CLK), .D(ADDR[31:2]), .Q(PC[31:2]));  // open: clr, up, carry
  Register #(.trigger("high"), .width(32)) register_1 (.D({PC[31:2], 2'b00}), .clk(1'b1));  // open: en, Q, clr

  assign PC[1:0] = 2'b00;
endmodule

module ArithmeticLogicUnit (
  input  [31:0] A,
  input  [31:0] PC,
  input  PCREL,
  input  [31:0] B,
  input  [4:0] SEL,
  input  [31:0] IMM,
  input  OPIMM,
  input  CLK,
  output [31:0] R,
  output RDY,
  output EQ,
  output LT,
  output LTU
);

  wire comparator_3_lt, comparator_4_lt, decoder_1_out0, decoder_1_out1, decoder_1_out2, decoder_1_out3,
       decoder_1_out4, decoder_1_out5, decoder_1_out6, decoder_1_out7, decoder_1_out8, decoder_1_out9,
       decoder_1_out10, decoder_1_out11, decoder_1_out12, decoder_1_out13, decoder_1_out14, decoder_1_out15,
       decoder_1_out16, decoder_1_out17, OVF;
  wire [31:0] ANDV, DIFF, multiplier_1_out, ORV, PROD, PRODH, PRODHSU, PRODHU, QUOT, QUOTU, REMS, REMU, SARV,
       shifter_1_out, shifter_2_out, shifter_3_out, SHLV, SHRV, SLTUV, SLTV, SUM, X, XORV, Y;
  wire [32:0] bit_extender_1_out, bit_extender_2_out;
  wire [32:31] multiplier_1_cout;

  assign bit_extender_1_out = {{1{X[31]}}, X};  // Bit_Extender bit_extender_1
  assign bit_extender_2_out = {{1{1'b0}}, Y};  // Bit_Extender bit_extender_2
  Multiplier #(.mode("twosComplement"), .width(33)) multiplier_1 (
    .a(bit_extender_1_out), .b(bit_extender_2_out), .out({PRODHSU[0], multiplier_1_out}),
    .cout({multiplier_1_cout, PRODHSU[31:1]}));  // open: cin
  Adder #(.width(32)) adder_1 (.a(X), .b(Y), .out(SUM));  // open: cin, cout
  Subtractor #(.width(32)) subtractor_1 (.a(X), .b(Y), .out(DIFF));  // open: bin, bout
  Multiplier #(.mode("twosComplement"), .width(32)) multiplier_2 (.a(X), .b(Y), .out(PROD), .cout(PRODH));  // open: cin
  Multiplier #(.width(32)) multiplier_3 (.a(X), .b(Y), .cout(PRODHU));  // open: out, cin
  Divider #(.mode("twosComplement"), .width(32)) divider_1 (.a(X), .b(Y), .out(QUOT), .rem(REMS));  // open: upper
  Divider #(.width(32)) divider_2 (.a(X), .b(Y), .out(QUOTU), .rem(REMU));  // open: upper
  LED F_EQ (.in(EQ));
  Comparator #(.width(32)) comparator_1 (.a(A), .b(B), .eq(EQ), .lt(LT));  // open: gt
  Comparator #(.mode("unsigned"), .width(32)) comparator_2 (.a(A), .b(B), .lt(LTU));  // open: gt, eq
  LED F_LT (.in(LT));
  Register #(.trigger("high"), .width(32)) u_SUM (.D(SUM), .clk(1'b1));  // open: en, Q, clr
  Register #(.trigger("high"), .width(32)) u_DIFF (.D(DIFF), .clk(1'b1));  // open: en, Q, clr
  Register #(.trigger("high"), .width(32)) u_PROD (.D(PROD), .clk(1'b1));  // open: en, Q, clr
  Register #(.trigger("high"), .width(32)) u_PRODH (.D(PRODH), .clk(1'b1));  // open: en, Q, clr
  Register #(.trigger("high"), .width(32)) u_PRODHU (.D(PRODHU), .clk(1'b1));  // open: en, Q, clr
  Register #(.trigger("high"), .width(32)) u_PRODHSU (.D(PRODHSU), .clk(1'b1));  // open: en, Q, clr
  Register #(.trigger("high"), .width(32)) u_QUOT (.D(QUOT), .clk(1'b1));  // open: en, Q, clr
  Register #(.trigger("high"), .width(32)) u_REMS (.D(REMS), .clk(1'b1));  // open: en, Q, clr
  Register #(.trigger("high"), .width(32)) u_QUOTU (.D(QUOTU), .clk(1'b1));  // open: en, Q, clr
  Register #(.trigger("high"), .width(32)) u_REMU (.D(REMU), .clk(1'b1));  // open: en, Q, clr
  LED F_LTU (.in(LTU));
  assign ORV = X | Y;  // OR_Gate or_1, 32 bits wide
  assign ANDV = X & Y;  // AND_Gate and_1, 32 bits wide
  assign XORV = X ^ Y;  // XOR_Gate xor_1, 32 bits wide
  Shifter #(.width(32)) shifter_1 (.in(X), .\dist (Y[4:0]), .out(shifter_1_out));
  Shifter #(.shift("lr"), .width(32)) shifter_2 (.in(X), .\dist (Y[4:0]), .out(shifter_2_out));
  Shifter #(.shift("ar"), .width(32)) shifter_3 (.in(X), .\dist (Y[4:0]), .out(shifter_3_out));
  Comparator #(.width(32)) comparator_3 (.a(X), .b(Y), .lt(comparator_3_lt));  // open: gt, eq
  Comparator #(.mode("unsigned"), .width(32)) comparator_4 (.a(X), .b(Y), .lt(comparator_4_lt));  // open: gt, eq
  Multiplexer #(.width(32)) multiplexer_1 (.in0(shifter_1_out), .in1({32{1'b0}}), .out(SHLV), .sel(OVF));
  Multiplexer #(.width(32)) multiplexer_2 (.in0(shifter_2_out), .in1({32{1'b0}}), .out(SHRV), .sel(OVF));
  Multiplexer #(.width(32)) multiplexer_3 (.in0(shifter_3_out), .in1({32{1'b0}}), .out(SARV), .sel(OVF));
  assign SLTV = {{31{1'b0}}, comparator_3_lt};  // Bit_Extender bit_extender_3
  assign SLTUV = {{31{1'b0}}, comparator_4_lt};  // Bit_Extender bit_extender_4
  Register #(.trigger("high"), .width(32)) u_ORV (.D(ORV), .clk(1'b1));  // open: en, Q, clr
  Register #(.trigger("high"), .width(32)) u_ANDV (.D(ANDV), .clk(1'b1));  // open: en, Q, clr
  Register #(.trigger("high"), .width(32)) u_XORV (.D(XORV), .clk(1'b1));  // open: en, Q, clr
  Register #(.trigger("high"), .width(32)) u_SHLV (.D(SHLV), .clk(1'b1));  // open: en, Q, clr
  Register #(.trigger("high"), .width(32)) u_SHRV (.D(SHRV), .clk(1'b1));  // open: en, Q, clr
  Register #(.trigger("high"), .width(32)) u_SARV (.D(SARV), .clk(1'b1));  // open: en, Q, clr
  Register #(.trigger("high"), .width(32)) u_SLTV (.D(SLTV), .clk(1'b1));  // open: en, Q, clr
  Register #(.trigger("high"), .width(32)) u_SLTUV (.D(SLTUV), .clk(1'b1));  // open: en, Q, clr
  LED F_SUM (.in(decoder_1_out0));
  LED F_DIFF (.in(decoder_1_out1));
  LED F_PROD (.in(decoder_1_out2));
  LED F_PRODH (.in(decoder_1_out3));
  LED F_PRODHU (.in(decoder_1_out4));
  LED F_PRODHSU (.in(decoder_1_out5));
  LED F_QUOT (.in(decoder_1_out6));
  LED F_REMS (.in(decoder_1_out7));
  LED F_QUOTU (.in(decoder_1_out8));
  LED F_REMU (.in(decoder_1_out9));
  LED F_ORV (.in(decoder_1_out10));
  LED F_ANDV (.in(decoder_1_out11));
  LED F_XORV (.in(decoder_1_out12));
  LED F_SHLV (.in(decoder_1_out13));
  LED F_SHRV (.in(decoder_1_out14));
  LED F_SARV (.in(decoder_1_out15));
  LED F_SLTV (.in(decoder_1_out16));
  LED F_SLTUV (.in(decoder_1_out17));
  Multiplexer #(.select(5), .width(32)) multiplexer_4 (
    .in0(SUM), .in1(DIFF), .in2(PROD), .in3(PRODH), .in4(PRODHU), .in5(PRODHSU), .in6(QUOT), .in7(REMS),
    .in8(QUOTU), .in9(REMU), .in10(ORV), .in11(ANDV), .in12(XORV), .in13(SHLV), .in14(SHRV), .in15(SARV),
    .in16(SLTV), .in17(SLTUV), .in18({32{1'b0}}), .in19({32{1'b0}}), .in20({32{1'b0}}), .in21({32{1'b0}}),
    .in22({32{1'b0}}), .in23({32{1'b0}}), .in24({32{1'b0}}), .in25({32{1'b0}}), .in26({32{1'b0}}),
    .in27({32{1'b0}}), .in28({32{1'b0}}), .in29({32{1'b0}}), .in30({32{1'b0}}), .in31({32{1'b0}}), .out(R),
    .sel(SEL));
  Decoder #(.enable("false"), .select(5)) decoder_1 (
    .out0(decoder_1_out0), .out1(decoder_1_out1), .out2(decoder_1_out2), .out3(decoder_1_out3),
    .out4(decoder_1_out4), .out5(decoder_1_out5), .out6(decoder_1_out6), .out7(decoder_1_out7),
    .out8(decoder_1_out8), .out9(decoder_1_out9), .out10(decoder_1_out10), .out11(decoder_1_out11),
    .out12(decoder_1_out12), .out13(decoder_1_out13), .out14(decoder_1_out14), .out15(decoder_1_out15),
    .out16(decoder_1_out16), .out17(decoder_1_out17), .sel(SEL));  // open: out18, out19, out20, out21, out22, out23, out24, out25, out26, out27, out28, out29, out30, out31
  Register #(.trigger("high"), .width(32)) VR (.D(R), .clk(1'b1));  // open: en, Q, clr
  or or_2 (OVF, Y[5], Y[6], Y[7], Y[8], Y[9], Y[10], Y[11], Y[12], Y[13], Y[14], Y[15], Y[16], Y[17], Y[18], Y[19], Y[20], Y[21], Y[22], Y[23], Y[24], Y[25], Y[26], Y[27], Y[28], Y[29], Y[30], Y[31]);
  Register #(.trigger("high"), .width(32)) VX (.D(X), .clk(1'b1));  // open: en, Q, clr
  Multiplexer #(.width(32)) multiplexer_5 (.in0(A), .in1(PC), .out(X), .sel(PCREL));
  LED #(.active("false")) X_A (.in(PCREL));
  LED X_PC (.in(PCREL));
  Register #(.trigger("high"), .width(32)) VY (.D(Y), .clk(1'b1));  // open: en, Q, clr
  Multiplexer #(.width(32)) multiplexer_6 (.in0(B), .in1(IMM), .out(Y), .sel(OPIMM));
  LED #(.active("false")) Y_B (.in(OPIMM));
  LED Y_IMM (.in(OPIMM));
  LED F_READY (.in(1'b1));

  assign RDY = 1'b1;

  // Other names for the same wires on the sheet: VX[31:0] = A; VY[31:0] = B; Y4_0[4:0] = Y[4:0]
endmodule

module MaskingUnit (
  input  M0,
  input  M1,
  input  M2,
  input  [31:0] DI,
  input  M3,
  output [31:0] DO
);

  wire [7:0] bit_extender_1_out, bit_extender_2_out, bit_extender_3_out, bit_extender_4_out;

  assign DO[7:0] = DI[7:0] & bit_extender_1_out;  // AND_Gate and_1, 8 bits wide
  assign bit_extender_1_out = {{7{M0}}, M0};  // Bit_Extender bit_extender_1
  assign DO[15:8] = DI[15:8] & bit_extender_2_out;  // AND_Gate and_2, 8 bits wide
  assign bit_extender_2_out = {{7{M1}}, M1};  // Bit_Extender bit_extender_2
  assign DO[23:16] = DI[23:16] & bit_extender_3_out;  // AND_Gate and_3, 8 bits wide
  assign bit_extender_3_out = {{7{M2}}, M2};  // Bit_Extender bit_extender_3
  assign DO[31:24] = DI[31:24] & bit_extender_4_out;  // AND_Gate and_4, 8 bits wide
  assign bit_extender_4_out = {{7{M3}}, M3};  // Bit_Extender bit_extender_4
endmodule

module LeftShifter (
  input  A0,
  input  A1,
  input  [31:0] DI,
  output [31:0] DO
);

  wire [31:0] multiplexer_1_out, shifter_1_out, shifter_2_out;

  Shifter #(.width(32)) shifter_1 (.in(DI), .\dist (5'b01000), .out(shifter_1_out));
  Multiplexer #(.width(32)) multiplexer_1 (.in0(DI), .in1(shifter_1_out), .out(multiplexer_1_out), .sel(A0));
  Multiplexer #(.width(32)) multiplexer_2 (.in0(multiplexer_1_out), .in1(shifter_2_out), .out(DO), .sel(A1));
  Shifter #(.width(32)) shifter_2 (.in(multiplexer_1_out), .\dist (5'b10000), .out(shifter_2_out));
endmodule

module RightShifter (
  input  A0,
  input  A1,
  input  [31:0] DI,
  output [31:0] DO
);

  wire [31:0] multiplexer_1_out, shifter_1_out, shifter_2_out;

  Shifter #(.shift("ar"), .width(32)) shifter_1 (.in(DI), .\dist (5'b01000), .out(shifter_1_out));
  Multiplexer #(.width(32)) multiplexer_1 (.in0(DI), .in1(shifter_1_out), .out(multiplexer_1_out), .sel(A0));
  Multiplexer #(.width(32)) multiplexer_2 (.in0(multiplexer_1_out), .in1(shifter_2_out), .out(DO), .sel(A1));
  Shifter #(.shift("lr"), .width(32)) shifter_2 (.in(multiplexer_1_out), .\dist (5'b10000), .out(shifter_2_out));
endmodule

module SignExtender (
  input  [31:0] DI,
  input  LB,
  input  LDSX,
  output [31:0] DO
);

  wire and_1_out;
  wire [6:0] bit_extender_1_out;
  wire [15:0] bit_extender_2_out;

  and and_1 (and_1_out, LB, LDSX);
  Multiplexer multiplexer_1 (.in0(DI[15]), .in1(DI[7]), .out(DO[15]), .sel(and_1_out));
  Multiplexer #(.width(7)) multiplexer_2 (.in0(DI[14:8]), .in1(bit_extender_1_out), .out(DO[14:8]), .sel(and_1_out));
  assign bit_extender_1_out = {{6{DI[7]}}, DI[7]};  // Bit_Extender bit_extender_1
  Multiplexer #(.width(16)) multiplexer_3 (.in0(DI[31:16]), .in1(bit_extender_2_out), .out(DO[31:16]), .sel(LDSX));
  assign bit_extender_2_out = {{15{DO[15]}}, DO[15]};  // Bit_Extender bit_extender_2

  assign DO[7:0] = DI[7:0];
endmodule

module BusInterface (
  input  [31:0] DI,
  input  [31:0] DOUT,
  input  RST,
  input  CLK,
  input  LDSX,
  input  LOAD0,
  input  LOAD1,
  input  STORE0,
  input  STORE1,
  input  [31:0] ADDR,
  output [31:0] DIN,
  output [31:0] DO,
  output STROBE,
  output EALIGN,
  output BM0,
  output BM1,
  output BM2,
  output BM3,
  output nRW,
  output [29:0] A
);

  wire LB, LD, not_1_out;
  wire [31:0] bit_extender_1_out, leftshifter_1_do, maskingunit_1_do, maskingunit_2_do, rightshifter_1_do,
       signextender_1_do;

  MaskingUnit maskingunit_1 (.DO(maskingunit_1_do), .DI(DI), .M0(BM0), .M1(BM1), .M2(BM2), .M3(BM3));
  LeftShifter leftshifter_1 (.DO(leftshifter_1_do), .DI(DOUT), .A0(ADDR[0]), .A1(ADDR[1]));
  MaskingUnit maskingunit_2 (.DO(maskingunit_2_do), .DI(leftshifter_1_do), .M0(BM0), .M1(BM1), .M2(BM2), .M3(BM3));
  not not_1 (not_1_out, CLK);
  // PlaRom #(.Contents("0*4 1 2 0*5 2 0*4 2 0*4 2 0*4 2 0*3 1 1 0 0 2 2 1 1 2 0 0 2 1 1 0 2 2 0 1 1 2 2 0 0 2 2 1 0 1 2*3 1 2 1 0 2 1 0 1 2 1 2 1 2 1 0 1 2 1 1 0 1 2 2 1 1 2 1 0 1 1 0 0 2 0 1 1 2 0*3 1 2 1 0 1 2 1 2 1 2 1 0 1 1 0*3 2 1 1 0 2 0*3 2 0 0 2 0 0 2 2 0*3 2 0*3 2*3 0 2 0 0 2 2 0 0 2 2 0 2 0 2 2 0 0 1 0*8 1 0*7 1 0*8 1 0*7 1 0*8 1 1 0*6 1 1 0*6 1 1 0*6 1 1 0*6 1 0*7 1 0*7 1 1 0*6 1 1 0*7 1 0*7 1 0*8 1 1 0*6 1 1 0*6 1 0*7 1 0*8 1 0*7 1 0*8 1 0*7 1 0*7 1 0*7 1 0*7 1 0*7 1"), .\and (27), .outputs(8)) MaskGen: pin names not known; wires that end beside it: {ADDR[1:0], STORE1, STORE0, LOAD1, LOAD0}, {LB, LD, nRW, BM3, BM2, BM1, BM0, EALIGN}
  Register #(.trigger("high"), .width(32)) MAR (.D(ADDR), .clk(1'b1));  // open: en, Q, clr
  RightShifter rightshifter_1 (.DO(rightshifter_1_do), .DI(maskingunit_1_do), .A0(ADDR[0]), .A1(ADDR[1]));
  nor nor_1 (STROBE, RST, not_1_out);
  SignExtender signextender_1 (.DO(signextender_1_do), .DI(rightshifter_1_do), .LB(LB), .LDSX(LDSX));
  Register #(.trigger("high"), .width(32)) MDO (.D(maskingunit_2_do), .clk(nRW));  // open: en, Q, clr
  assign DO = nRW ? maskingunit_2_do : 32'bz;  // Controlled_Buffer controlled_buffer_1
  assign bit_extender_1_out = {{31{LD}}, LD};  // Bit_Extender bit_extender_1
  assign DIN = bit_extender_1_out & signextender_1_do;  // AND_Gate and_1, 32 bits wide
  Register #(.trigger("high"), .width(32)) MDI (.D(DIN), .clk(1'b1));  // open: en, Q, clr

  assign A = ADDR[31:2];

  // Other names for the same wires on the sheet: A0 = ADDR[0]; A1 = ADDR[1]; M0 = BM0; M1 = BM1; M2 = BM2; M3 = BM3;
  //   ST = nRW; SX = LDSX

  // Notes on the sheet:
  //   RST: pull=up
endmodule

module FetchUnit (
  input  IRQ,
  input  HOLD,
  input  [31:0] DIN,
  input  SX,
  input  [31:0] EMA,
  input  LD0,
  input  [31:0] PC_IN,
  input  LD1,
  input  ST0,
  input  ST1,
  input  CLK,
  output GRANT,
  output [31:0] INSTR,
  output PCE,
  output LDSX,
  output [31:0] ADDR,
  output LOAD0,
  output LOAD,
  output LOAD1,
  output [31:0] PC,
  output STORE0,
  output STORE1
);

  wire and_1_out, IRQ_t, not_1_out, not_2_out, or_2_out, PCE_t, PCM;
  wire [31:0] multiplexer_3_out;

  or or_1 (PCM, or_2_out, LOAD);
  or or_2 (or_2_out, ST1, ST0);
  and and_1 (and_1_out, IRQ, not_1_out);
  not not_1 (not_1_out, HOLD);
  nor nor_1 (PCE, PCM, HOLD, and_1_out);
  or or_3 (LOAD, LD1, LD0);
  D_Flip_Flop d_ff_1 (.D(and_1_out), .clk(CLK), .Q(GRANT));  // open: Qn, preset, reset
  or or_4 (PCE_t, and_1_out, PCE);
  LED FETCHING (.in(PCE));
  and and_2 (LDSX, LOAD, SX);
  Multiplexer multiplexer_1 (.in0(PCE), .in1(LD0), .out(LOAD0), .sel(LOAD));
  Multiplexer multiplexer_2 (.in0(PCE), .in1(LD1), .out(LOAD1), .sel(LOAD));
  or or_5 (IRQ_t, and_1_out, GRANT);
  Register #(.width(32)) INS (.D(multiplexer_3_out), .en(PCE_t), .clk(CLK), .Q(INSTR));  // open: clr
  Multiplexer #(.width(32)) multiplexer_3 (.in0(DIN), .in1(32'h13), .out(multiplexer_3_out), .sel(IRQ_t));
  Register #(.width(32)) PCR (.D(PC_IN), .en(PCE_t), .clk(CLK), .Q(PC));  // open: clr
  not not_2 (not_2_out, PCM);
  Multiplexer #(.width(32)) multiplexer_4 (.in0(EMA), .in1(PC_IN), .out(ADDR), .sel(not_2_out));

  assign STORE0 = ST0;
  assign STORE1 = ST1;
endmodule

module InstructionDecoder (
  input  [31:0] INSTR,
  input  EQ,
  input  LT,
  input  READY,
  input  LTU,
  input  CLK,
  input  RST,
  output WFI,
  output SYS,
  output [4:0] RD,
  output [4:0] RS1,
  output [4:0] RS2,
  output [11:0] CSRI,
  output RET,
  output BRK,
  output [4:0] ALU_OP,
  output PCREL,
  output OPIMM,
  output BRANCH,
  output LINK,
  output SX,
  output LD0,
  output ILL,
  output LD1,
  output ST0,
  output ST1,
  output CSR_EN,
  output CSR_BIT,
  output CSR_CLR,
  output [31:0] IMM,
  output HOLD
);

  wire and_11_out, and_16_out, and_17_out, BR, BRK_t, COND, CSRI_t, CTR, DE, EMC, FUNCT, HLD, ILL_D, ILL_S,
       multiplexer_3_out, multiplexer_4_out, nand_2_out, not_1_out, nSHIFT, or_3_out, or_4_out, REG_WE,
       RET_t, S0, S1E, S2E, S4_1_0, S4_1_1, S10_5, S19_12, S30_20, SYS_t, WFI_t, X0, X11, xor_1_out;
  wire [3:0] and_8_out, and_9_out, or_2_out;
  wire [4:0] or_1_out;
  wire [4:4] and_1_out, nand_1_out;
  wire [5:0] and_10_out;
  wire [5:5] and_6_out;
  wire [7:0] multiplexer_1_out;
  wire [8:3] CLF_p2;
  wire [10:0] multiplexer_2_out;
  wire [11:0] bit_extender_1_out;
  wire [18:0] bit_extender_2_out;
  wire [31:0] bit_extender_3_out;

  Register #(.trigger("high"), .width(32)) V_INS (.D(INSTR), .clk(1'b1));  // open: en, Q, clr
  and and_1 (and_1_out[4], DE, REG_WE);
  assign RD = {5{and_1_out[4]}} & INSTR[11:7];  // AND_Gate and_2, 5 bits wide
  nand nand_1 (nand_1_out[4], INSTR[0], INSTR[1]);
  Register #(.trigger("high"), .width(5)) V_RD (.D(RD), .clk(1'b1));  // open: en, Q, clr
  assign or_1_out = {5{nand_1_out[4]}} | INSTR[6:2];  // OR_Gate or_1, 5 bits wide
  ROM #(.addrWidth(11), .dataWidth(24)) rom_1 (
    .addr({CTR, COND, INSTR[25], INSTR[14:12], or_1_out}),
    .data({ILL_D, HLD, SYS_t, FUNCT, nSHIFT, CSR_CLR, CSR_BIT, CSRI_t, CSR_EN, ST1, ST0, LD1, LD0, SX, LINK, BRANCH, OPIMM, PCREL, REG_WE, ALU_OP}));
  // PlaRom #(.Contents("0 2 0 2 2 1 1 2 0 2 0 2*3 1 1 0 2 0 1 1 0 1 1 0 2 0 1*3 2 2 0 0 2 1 2 1*3 0*3 2 2 1 0 2 0*3 2*3 1 1 0*3 1 1 0 1 1 0*3 1*3 2 2 0*4 2 1*3 0*3 2 2 0 1 1 0*3 1 0 1*3 0 2 0 2 2 1 2*3 0 0 2 2 1 1 2 2 0 0 2*3 1 1 2 0 0 1 0 1*3 2 0 0 1 1 0 1 1 2 0 0 1*3 2 2 0 0 2*3 1*3 0*3 1 0 2 1 2 0*3 2 2 1 2 2 1 0*6 1 0*6 1 0*6 1 0*6 1 0*7 1 0 1 0*4 1 0*6 1 0 1 0*4 1 0 1 0*5 1 0*7 1 0*6 1 0*7 1 0*6 1 0*6 1 0*6 1 0*6 1 0*6 1 0*6 1 0*7 1 1 0*5 1 0"), .\and (21), .outputs(7)) IDEC: pin names not known; wires that end beside it: {INSTR[31], INSTR[20], INSTR[7:2]}, {X0, S4_1_0, S4_1_1, S10_5, X11, S19_12, S30_20}
  // PlaRom #(.Contents("1*9 2*3 1 2 1 1 2 2 1 2 0*3 2 2 0 1 0 2 0*3 2 0 1 0 1 2 0 0 2 0 0 1 0 1 2 1 0 0 1 0*5 1 0*5 1 0*5 1 0*5 1 0*4 1 0*4 1 0*4 1 0*4 1 0*4 1"), .\and (10), .outputs(5)) SDEC: pin names not known; wires that end beside it: {INSTR[29:28], INSTR[22:20]}, {EMC, BRK_t, RET_t, WFI_t, ILL_S}
  // PlaRom #(.Contents("0*3 1 2 2 1 1 0*3 2 2 1 1 2 0*3 2*3 1 1 0*3 1 1 0 1 1 0*3 1*3 2 2 0*3 1 2 1*3 0*3 2 2 1*3 0*3 1 0 2 1 2 0*3 2 2 1 2 2 0*3 1 0 0 1 1 0*3 2 2 1 1 0 1 0*3 2 0 1 1 0 1 1 0 2 0 1 1 0*4 2 1*3 0*3 1 2 0 1 1 0*3 1 0 2 1 0*4 2 2 1 0 2 0*4 2 2 1 1 1 0*9 1 0*8 1 0*8 1 0*6 1 0 1 0*4 1 0 1 0 0 1 0*9 1 0*9 1 0*9 1 0*9 1 0*8 1 0*8 1 0*8 1 0*9 1 0*8 1 0*9 1 0*8 1 0*8 1"), .\and (18), .outputs(9)) CLF: pin names not known; wires that end beside it: {INSTR[14:12], INSTR[6:2]}, {CLF_p2[8:6], BR, CLF_p2[4:3], S1E, S2E, DE}
  assign RS1 = {5{S1E}} & INSTR[19:15];  // AND_Gate and_3, 5 bits wide
  LED J (.in(CLF_p2[3]));
  LED U (.in(CLF_p2[4]));
  LED B (.in(BR));
  LED S (.in(CLF_p2[6]));
  LED I (.in(CLF_p2[7]));
  LED R (.in(CLF_p2[8]));
  Register #(.trigger("high"), .width(5)) V_RS1 (.D(RS1), .clk(1'b1));  // open: en, Q, clr
  assign RS2 = {5{S2E}} & INSTR[24:20];  // AND_Gate and_4, 5 bits wide
  nand nand_2 (nand_2_out, READY, CTR);
  and and_5 (HOLD, nand_2_out, HLD);
  Register #(.trigger("high"), .width(5)) V_RS2 (.D(RS2), .clk(1'b1));  // open: en, Q, clr
  D_Flip_Flop d_ff_1 (.D(HOLD), .clk(CLK), .Q(CTR), .Qn(S0), .reset(RST));  // open: preset
  LED S1 (.in(CTR));
  LED u_S0 (.in(S0));
  assign bit_extender_1_out = {{11{CSR_EN}}, CSR_EN};  // Bit_Extender bit_extender_1
  and and_6 (and_6_out[5], S10_5, nSHIFT);
  assign bit_extender_2_out = {{18{INSTR[31]}}, INSTR[31]};  // Bit_Extender bit_extender_2
  Register #(.trigger("high"), .width(12)) V_CSRI (.D(CSRI), .clk(1'b1));  // open: en, Q, clr
  assign CSRI = INSTR[31:20] & bit_extender_1_out;  // AND_Gate and_7, 12 bits wide
  assign and_8_out = {4{S4_1_1}} & INSTR[11:8];  // AND_Gate and_8, 4 bits wide
  assign and_9_out = INSTR[24:21] & {4{S4_1_0}};  // AND_Gate and_9, 4 bits wide
  not not_1 (not_1_out, S19_12);
  Multiplexer #(.width(8)) multiplexer_1 (
    .in0(INSTR[19:12]), .in1(bit_extender_2_out[7:0]), .out(multiplexer_1_out), .sel(not_1_out));
  Multiplexer #(.width(11)) multiplexer_2 (
    .in0(bit_extender_2_out[18:8]), .in1(INSTR[30:20]), .out(multiplexer_2_out), .sel(S30_20));
  Multiplexer multiplexer_3 (.in0(EQ), .in1(LT), .out(multiplexer_3_out), .sel(INSTR[14]));
  Multiplexer multiplexer_4 (.in0(multiplexer_3_out), .in1(LTU), .out(multiplexer_4_out), .sel(INSTR[13]));
  assign or_2_out = and_8_out | and_9_out;  // OR_Gate or_2, 4 bits wide
  assign and_10_out = INSTR[30:25] & {6{and_6_out[5]}};  // AND_Gate and_10, 6 bits wide
  Multiplexer #(.width(32)) multiplexer_5 (
    .in0({INSTR[31], multiplexer_2_out, multiplexer_1_out, X11, and_10_out, or_2_out, X0}),
    .in1(bit_extender_3_out), .out(IMM), .sel(CSRI_t));
  assign bit_extender_3_out = {{27{1'b0}}, INSTR[19:15]};  // Bit_Extender bit_extender_3
  xor xor_1 (xor_1_out, INSTR[12], multiplexer_4_out);
  and and_11 (and_11_out, xor_1_out, BR);
  LED u_COND (.in(and_11_out));
  Register #(.trigger("high"), .width(32)) V_IMM (.D(IMM), .clk(1'b1));  // open: en, Q, clr
  Multiplexer multiplexer_6 (.in0(INSTR[30]), .in1(xor_1_out), .out(COND), .sel(BR));
  or or_3 (or_3_out, INSTR[31], INSTR[25], INSTR[7], INSTR[8], INSTR[9], INSTR[10], INSTR[11], INSTR[15], INSTR[16], INSTR[17], INSTR[18], INSTR[19], INSTR[23], INSTR[24], INSTR[26], INSTR[27], ILL_S);
  or or_4 (or_4_out, INSTR[31], INSTR[26], INSTR[27], INSTR[28], INSTR[29]);
  and and_12 (WFI, WFI_t, SYS_t);
  and and_13 (SYS, EMC, S0, SYS_t);
  and and_14 (RET, SYS_t, S0, RET_t);
  and and_15 (BRK, S0, BRK_t, SYS_t);
  and and_16 (and_16_out, SYS_t, or_3_out);
  or or_5 (ILL, and_16_out, ILL_D, and_17_out);
  and and_17 (and_17_out, or_4_out, FUNCT);

  // Other names for the same wires on the sheet: P7 = INSTR[7]; P11_7[4:0] = INSTR[11:7]; OP[4:0] = INSTR[6:2];
  //   CSR = CSR_EN; P14_12[2:0] = INSTR[14:12]; P19_15[4:0] = INSTR[19:15]; P20 = INSTR[20];
  //   P22_20[2:0] = INSTR[22:20]; P24_20[4:0] = INSTR[24:20]; P24_21[3:0] = INSTR[24:21]; P24_23[1:0] = INSTR[24:23];
  //   P25 = INSTR[25]; P30_25[5:0] = INSTR[30:25]; P27_26[1:0] = INSTR[27:26]; P29_26[3:0] = INSTR[29:26];
  //   P29_28[1:0] = INSTR[29:28]; P30 = INSTR[30]; P31 = INSTR[31]; P11_8[3:0] = INSTR[11:8]

  // Notes on the sheet:
  //   OP [0]
  //   OP [1]
  //   OP [6:2]
  //   rd/imm [11:7]
  //   funct3/imm [14:12]
  //   rs1/imm [19:15]
  //   rs2/imm [24:20]
  //   funct7/imm [31:25]
  //   contents of rom_1 (hex, n*v repeats v):
  //   480ca0 800000 800000 80000 800a0 800e0 800000 800000 482080 800000 800000 800000 180020 800a0
  //   10*800000 80000 4803a0 800000 4803e0 680000 800000 800000 800000 4814a0 800000 800000 80000 1000ad
  //   800e0 800000 800000 484080 800000 800000 800000 10002d 800a0 10*800000 80000 800000 800000 4803e0
  //   88020 800000 800000 800000 4818a0 800000 800000 800000 800b0 800e0 800000 800000 486080 800000
  //   800000 800000 180030 800a0 13*800000 4803e0 a8020 7*800000 800b1 800e0 6*800000 180031 800a0
  //   13*800000 4803e0 e8020 800000 800000 800000 4808a0 800000 800000 800000 800ac 800e0 6*800000 18002c
  //   800a0 10*800000 80000 800000 800000 4803e0 4*800000 4810a0 800000 800000 800000 1000ae 800e0
  //   6*800000 10002e 800a0 10*800000 80000 800000 800000 4803e0 980a0 7*800000 800aa 800e0 6*800000
  //   18002a 800a0 10*800000 80000 800000 800000 4803e0 b80a0 7*800000 800ab 800e0 6*800000 18002b 800a0
  //   10*800000 80000 800000 800000 4803e0 f80a0 800000 800000 800000 480ca0 800000 800000 80000 800a0
  //   800e0 800000 800000 482080 800000 800000 800000 180022 800a0 10*800000 80000 4803a0 800000 4803e0
  //   680000 800000 800000 800000 4814a0 800000 800000 80000 800000 800e0 800000 800000 484080 800000
  //   800000 800000 180023 800a0 10*800000 80000 800000 800000 4803e0 88020 800000 800000 800000 4818a0
  //   800000 800000 800000 800b0 800e0 800000 800000 486080 800000 800000 800000 180025 800a0 13*800000
  //   4803e0 a8020 7*800000 800b1 800e0 6*800000 180024 800a0 13*800000 4803e0 e8020 800000 800000 800000
  //   4808a0 800000 800000 800000 800ac 800e0 6*800000 180026 800a0 10*800000 80000 800000 800000 4803e0
  //   4*800000 4810a0 4*800000 800e0 6*800000 180027 800a0 10*800000 80000 800000 800000 4803e0 980a0
  //   7*800000 800aa 800e0 6*800000 180028 800a0 10*800000 80000 800000 800000 4803e0 b80a0 7*800000 800ab
  //   800e0 6*800000 180029 800a0 10*800000 80000 800000 800000 4803e0 f80a0 800000 800000 800000 480ca0
  //   800000 800000 80000 800a0 800e0 800000 800000 482080 800000 800000 800000 180021 800a0 10*800000
  //   4801c0 4803a0 800000 4803e0 4*800000 4814a0 800000 800000 80000 800000 800e0 800000 800000 484080
  //   4*800000 800a0 10*800000 4801c0 800000 800000 4803e0 88020 800000 800000 800000 4818a0 800000 800000
  //   800000 800b0 800e0 800000 800000 486080 4*800000 800a0 13*800000 4803e0 a8020 7*800000 800b1 800e0
  //   7*800000 800a0 13*800000 4803e0 e8020 800000 800000 800000 4808a0 800000 800000 800000 800ac 800e0
  //   7*800000 800a0 10*800000 4801c0 800000 800000 4803e0 4*800000 4810a0 800000 800000 800000 1000af
  //   800e0 6*800000 10002f 800a0 10*800000 4801c0 800000 800000 4803e0 980a0 7*800000 800aa 800e0
  //   7*800000 800a0 10*800000 4801c0 800000 800000 4803e0 b80a0 7*800000 800ab 800e0 7*800000 800a0
  //   10*800000 4801c0 800000 800000 4803e0 f80a0 800000 800000 800000 480ca0 800000 800000 80000 800a0
  //   800e0 800000 800000 482080 4*800000 800a0 10*800000 4801c0 4803a0 800000 4803e0 4*800000 4814a0
  //   800000 800000 80000 800000 800e0 800000 800000 484080 4*800000 800a0 10*800000 4801c0 800000 800000
  //   4803e0 88020 800000 800000 800000 4818a0 800000 800000 800000 800b0 800e0 800000 800000 486080
  //   4*800000 800a0 13*800000 4803e0 a8020 7*800000 800b1 800e0 7*800000 800a0 13*800000 4803e0 e8020
  //   800000 800000 800000 4808a0 800000 800000 800000 800ac 800e0 7*800000 800a0 10*800000 4801c0 800000
  //   800000 4803e0 4*800000 4810a0 4*800000 800e0 7*800000 800a0 10*800000 4801c0 800000 800000 4803e0
  //   980a0 7*800000 800aa 800e0 7*800000 800a0 10*800000 4801c0 800000 800000 4803e0 b80a0 7*800000 800ab
  //   800e0 7*800000 800a0 10*800000 4801c0 800000 800000 4803e0 f80a0 800000 800000 800000 80000 7*800000
  //   80000 15*800000 80000 80000 800000 80000 680000 800000 800000 800000 80000 7*800000 80000 15*800000
  //   80000 800000 800000 80000 4*800000 80000 7*800000 80000 18*800000 80000 31*800000 80000 4*800000
  //   80000 23*800000 80000 800000 800000 80000 4*800000 80000 23*800000 80000 800000 800000 80000
  //   28*800000 80000 800000 800000 80000 28*800000 80000 800000 800000 80000 4*800000 80000 7*800000
  //   80000 15*800000 80000 80000 800000 80000 680000 800000 800000 800000 80000 7*800000 80000 15*800000
  //   8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
endmodule

module ResultMux (
  input  [31:0] ALU,
  input  [31:0] NPC,
  input  [31:0] MDI,
  input  [31:0] CSR,
  input  LINK,
  input  LOAD,
  input  LDCSR,
  output [31:0] RES
);

  wire and_1_out, and_2_out, and_3_out, not_1_out, not_2_out, not_3_out;

  Register #(.trigger("high"), .width(32)) V_ALU (.D(ALU), .clk(1'b1));  // open: en, Q, clr
  Register #(.trigger("high"), .width(32)) V_NPC (.D(NPC), .clk(1'b1));  // open: en, Q, clr
  Register #(.trigger("high"), .width(32)) V_MDI (.D(MDI), .clk(1'b1));  // open: en, Q, clr
  Register #(.trigger("high"), .width(32)) V_CSR (.D(CSR), .clk(1'b1));  // open: en, Q, clr
  assign RES = and_1_out ? ALU : 32'bz;  // Controlled_Buffer controlled_buffer_1
  LED S_ALU (.in(and_1_out));
  LED S_NPC (.in(and_2_out));
  LED S_MDI (.in(and_3_out));
  LED S_CSR (.in(LDCSR));
  and and_1 (and_1_out, not_1_out, not_2_out, not_3_out);
  not not_1 (not_1_out, LINK);
  not not_2 (not_2_out, LOAD);
  not not_3 (not_3_out, LDCSR);
  assign RES = and_2_out ? NPC : 32'bz;  // Controlled_Buffer controlled_buffer_2
  assign RES = and_3_out ? MDI : 32'bz;  // Controlled_Buffer controlled_buffer_3
  and and_2 (and_2_out, LINK, not_2_out, not_3_out);
  and and_3 (and_3_out, LOAD, not_3_out);
  assign RES = LDCSR ? CSR : 32'bz;  // Controlled_Buffer controlled_buffer_4
endmodule

module ControlStatusRegisters (
  input  CLR,
  input  RST,
  input  [31:0] PC,
  input  IRET,
  input  [31:0] CAUSE_IN,
  input  TRAP,
  input  CLK,
  input  OPIMM,
  input  [31:0] RX,
  input  [31:0] IMM,
  input  [11:0] CSR,
  input  BIT,
  input  CSE,
  input  ILL_IN,
  output [31:0] EPC,
  output [31:0] ISR,
  output [31:0] CSR_OUT,
  output EIE,
  output LDCSR,
  output ILL
);

  wire and_5_out, and_8_out, and_9_out, and_10_out, and_11_out, and_12_out, and_13_out, and_14_out,
       and_15_out, and_16_out, and_17_out, comparator_1_eq, decoder_1_out0, decoder_1_out1, decoder_1_out2,
       decoder_1_out3, decoder_1_out4, decoder_1_out6, EPC_t, MIE, not_4_out, not_5_out, not_6_out, or_3_out,
       or_4_out, or_5_out, RES, STR, STW, TMP, VEC, WR;
  wire [1:0] or_2_out;
  wire [4:0] rom_1_data;
  wire [7:3] STX;
  wire [29:0] multiplexer_4_out, or_2_out_2;
  wire [31:0] and_2_out, and_3_out, and_4_out, bit_extender_1_out, bit_extender_2_out, CSRV, IEV,
       multiplexer_2_out, multiplexer_3_out, not_1_out, not_2_out, not_3_out, R_CAUSE_q, R_TEMP_q, STV;

  assign bit_extender_1_out = {{31{BIT}}, BIT};  // Bit_Extender bit_extender_1
  assign bit_extender_2_out = {{31{CLR}}, CLR};  // Bit_Extender bit_extender_2
  LED S_MIE (.in(STV[3]));
  LED S_MPIE (.in(STV[7]));
  or or_1 (STW, IRET, TRAP);
  LED #(.active("false")) F_REG (.in(OPIMM));
  Register #(.trigger("high"), .width(32)) V_IN (.D(CSRV), .clk(1'b1));  // open: en, Q, clr
  assign not_1_out = ~CSRV;  // NOT_Gate not_1, 32 bits wide
  assign not_2_out = ~bit_extender_1_out;  // NOT_Gate not_2, 32 bits wide
  assign not_3_out = ~bit_extender_2_out;  // NOT_Gate not_3, 32 bits wide
  and and_1 (EIE, IEV[11], STV[3]);
  LED F_IMM (.in(OPIMM));
  Multiplexer #(.width(32)) multiplexer_1 (.in0(RX), .in1(IMM), .out(CSRV), .sel(OPIMM));
  Register #(.trigger("high"), .width(12)) V_CSR (.D(CSR), .clk(1'b1));  // open: en, Q, clr
  assign and_2_out = bit_extender_1_out & CSR_OUT & not_1_out;  // AND_Gate and_2, 32 bits wide
  assign and_3_out = CSRV & not_2_out;  // AND_Gate and_3, 32 bits wide
  assign and_4_out = CSRV & not_3_out;  // AND_Gate and_4, 32 bits wide
  Comparator #(.mode("unsigned"), .width(32)) comparator_1 (
    .a(CSRV), .b({32{1'b0}}), .eq(comparator_1_eq));  // open: gt, lt
  and and_5 (and_5_out, comparator_1_eq, BIT);
  assign {or_2_out_2, or_2_out} = and_2_out | and_3_out | and_4_out;  // OR_Gate or_2, 32 bits wide
  not not_4 (not_4_out, and_5_out);
  and and_6 (WR, not_4_out, CSE);
  and and_7 (LDCSR, and_5_out, CSE);
  Multiplexer #(.width(32)) multiplexer_2 (
    .in0({or_2_out_2, or_2_out}), .in1({STV[31:8], STX[7], STV[6:4], STX[3], STV[2:0]}),
    .out(multiplexer_2_out), .sel(STW));
  and and_8 (and_8_out, STR, WR);
  Multiplexer #(.width(32)) multiplexer_3 (.in0({or_2_out_2, or_2_out}), .in1(PC), .out(multiplexer_3_out), .sel(TRAP));
  and and_9 (and_9_out, EPC_t, WR);
  LED F_WR (.in(WR));
  // Probe on multiplexer_2_out
  Register #(.width(32)) R_STATUS (.D(multiplexer_2_out), .en(or_3_out), .clk(CLK), .Q(STV));  // open: clr
  or or_3 (or_3_out, STW, and_8_out);
  Register #(.width(32)) R_IE (.D({or_2_out_2, or_2_out}), .en(and_10_out), .clk(CLK), .Q(IEV));  // open: clr
  and and_10 (and_10_out, MIE, WR);
  Register #(.width(32)) R_TEMP (.D({or_2_out_2, or_2_out}), .en(and_11_out), .clk(CLK), .Q(R_TEMP_q));  // open: clr
  and and_11 (and_11_out, WR, TMP);
  Register #(.width(32)) R_EPC (.D(multiplexer_3_out), .en(or_4_out), .clk(CLK), .Q(EPC));  // open: clr
  or or_4 (or_4_out, TRAP, and_9_out);
  Register #(.width(32)) R_CAUSE (.D(CAUSE_IN), .en(TRAP), .clk(CLK), .Q(R_CAUSE_q));  // open: clr
  ROM #(.addrWidth(13), .dataWidth(5)) rom_1 (.addr({WR, CSR}), .data(rom_1_data));
  assign CSR_OUT = STR ? STV : 32'bz;  // Controlled_Buffer controlled_buffer_1
  assign CSR_OUT = MIE ? IEV : 32'bz;  // Controlled_Buffer controlled_buffer_2
  assign CSR_OUT = TMP ? R_TEMP_q : 32'bz;  // Controlled_Buffer controlled_buffer_3
  assign CSR_OUT = EPC_t ? EPC : 32'bz;  // Controlled_Buffer controlled_buffer_4
  assign CSR_OUT = RES ? R_CAUSE_q : 32'bz;  // Controlled_Buffer controlled_buffer_5
  not not_5 (not_5_out, IRET);
  not not_6 (not_6_out, TRAP);
  Multiplexer #(.width(30)) multiplexer_4 (.in0(or_2_out_2), .in1(30'h3fffffc0), .out(multiplexer_4_out), .sel(RST));
  and and_12 (and_12_out, WR, VEC);
  assign CSR_OUT = decoder_1_out0 ? {32{1'b0}} : 32'bz;  // Controlled_Buffer controlled_buffer_6
  and and_13 (and_13_out, IRET, STV[7]);
  and and_14 (and_14_out, STV[3], not_5_out, not_6_out);
  and and_15 (and_15_out, not_6_out, STV[7]);
  and and_16 (and_16_out, STV[3], TRAP);
  Register #(.width(32)) R_VEC (.D({multiplexer_4_out, 2'b00}), .en(or_5_out), .clk(CLK), .Q(ISR));  // open: clr
  or or_5 (or_5_out, RST, and_12_out);
  assign CSR_OUT = decoder_1_out1 ? 32'h63687a79 : 32'bz;  // Controlled_Buffer controlled_buffer_7
  assign CSR_OUT = decoder_1_out2 ? 32'h1000 : 32'bz;  // Controlled_Buffer controlled_buffer_8
  assign CSR_OUT = decoder_1_out3 ? 32'h1 : 32'bz;  // Controlled_Buffer controlled_buffer_9
  assign CSR_OUT = decoder_1_out4 ? {32{1'b0}} : 32'bz;  // Controlled_Buffer controlled_buffer_10
  Decoder #(.enable("false"), .select(4)) decoder_1 (
    .out0(decoder_1_out0), .out1(decoder_1_out1), .out2(decoder_1_out2), .out3(decoder_1_out3),
    .out4(decoder_1_out4), .out5(STR), .out6(decoder_1_out6), .out7(MIE), .out8(VEC), .out9(TMP),
    .out10(EPC_t), .out11(RES), .sel(rom_1_data[3:0]));  // open: out12, out13, out14, out15
  or or_6 (STX[3], and_13_out, and_14_out);
  or or_7 (STX[7], and_15_out, and_16_out);
  assign CSR_OUT = VEC ? ISR : 32'bz;  // Controlled_Buffer controlled_buffer_11
  assign CSR_OUT = decoder_1_out6 ? 32'h40001100 : 32'bz;  // Controlled_Buffer controlled_buffer_12
  and and_17 (and_17_out, CSE, rom_1_data[4]);
  or or_8 (ILL, and_17_out, ILL_IN);
  LED F_STR (.in(STR));
  LED F_MIE (.in(MIE));
  LED F_VEC (.in(VEC));
  LED F_TMP (.in(TMP));
  LED F_EPC (.in(EPC_t));
  LED F_RES (.in(RES));

  // Other names for the same wires on the sheet: INT = TRAP; PCV[31:0] = EPC; RET = IRET;
  //   STX (some bits) = {STV[31:8], STV[6:4], STV[2:0]}; VFB[31:0] = CSR_OUT

  // Notes on the sheet:
  //   contents of rom_1 (hex, n*v repeats v):
  //   768*10 5 6 10 10 7 8 58*10 9 a b 3022*10 1 2 3 4 1003*10 5 6 10 10 7 8 58*10 9 a b 3261*10
endmodule

module InterruptController (
  input  TRIG,
  input  GRANT,
  input  CLK,
  input  RDY_IN,
  input  WFI,
  input  EIE,
  input  LDR,
  input  JMP,
  input  EAL,
  input  RET,
  input  EPL,
  input  ILL,
  input  SYS,
  input  BRK,
  input  RST,
  input  [31:0] ALU,
  input  [31:0] EPC,
  input  [31:0] ISR,
  output IRQ,
  output RDY,
  output SET,
  output TRAP,
  output [31:0] CAUSE,
  output [31:0] REF
);

  wire and_2_out, CLI, d_ff_1_q, d_ff_1_qn, d_ff_2_q, decoder_1_out0, decoder_1_out1, decoder_1_out2,
       decoder_1_out3, decoder_1_out4, decoder_1_out5, decoder_1_out6, decoder_1_out7, EAL_t, EINT, ESL, IRG,
       j_k_ff_1_q, nand_1_out, not_1_out, not_2_out, not_3_out, or_2_out, or_4_out, or_5_out, TRIG_t;
  wire [2:0] priority_encoder_1_out;
  wire [31:0] multiplexer_1_out;

  J_K_Flip_Flop j_k_ff_1 (.J(1'b0), .K(1'b1), .clk(CLK), .Q(j_k_ff_1_q), .preset(TRIG));  // open: Qn, reset
  LED F_EIE (.in(EIE));
  and and_1 (EINT, EIE, TRIG_t, not_1_out);
  not not_1 (not_1_out, or_2_out);
  or or_1 (SET, or_2_out, JMP);
  or or_2 (or_2_out, RET, TRAP);
  or or_3 (TRAP, IRG, SYS, BRK);
  Multiplexer #(.width(32)) multiplexer_1 (.in0(ALU), .in1(EPC), .out(multiplexer_1_out), .sel(RET));
  Multiplexer #(.width(32)) multiplexer_2 (.in0(multiplexer_1_out), .in1(ISR), .out(REF), .sel(TRAP));
  LED F_TRIG (.in(or_4_out));
  or or_4 (or_4_out, j_k_ff_1_q, TRIG_t);
  J_K_Flip_Flop j_k_ff_2 (.J(j_k_ff_1_q), .K(1'b0), .clk(CLK), .Q(TRIG_t), .reset(CLI));  // open: Qn, preset
  LED F_JMP (.in(SET));
  LED F_IRQ (.in(TRAP));
  Register #(.trigger("high"), .width(32)) V_REF (.D(REF), .clk(1'b1));  // open: en, Q, clr
  not not_2 (not_2_out, WFI);
  and and_2 (and_2_out, WFI, EINT);
  not not_3 (not_3_out, LDR);
  and and_3 (RDY, RDY_IN, or_5_out);
  or or_5 (or_5_out, not_2_out, and_2_out);
  and and_4 (EAL_t, not_3_out, EAL);
  and and_5 (ESL, LDR, EAL);
  nand nand_1 (nand_1_out, d_ff_1_q, GRANT);
  D_Flip_Flop d_ff_1 (.D(nand_1_out), .clk(CLK), .Q(d_ff_1_q), .Qn(d_ff_1_qn), .preset(d_ff_2_q));  // open: reset
  D_Flip_Flop d_ff_2 (.D(d_ff_1_qn), .clk(CLK), .Q(d_ff_2_q), .reset(d_ff_2_q));  // open: Qn, preset
  Decoder #(.enable("false"), .select(3)) decoder_1 (
    .out0(decoder_1_out0), .out1(decoder_1_out1), .out2(decoder_1_out2), .out3(decoder_1_out3),
    .out4(decoder_1_out4), .out5(decoder_1_out5), .out6(decoder_1_out6), .out7(decoder_1_out7),
    .sel(priority_encoder_1_out));
  Priority_Encoder priority_encoder_1 (
    .in0(1'b1), .in1(TRIG_t), .in2(EAL_t), .in3(ESL), .in4(BRK), .in5(SYS), .in6(EPL), .in7(ILL),
    .out(priority_encoder_1_out));  // open: en_in, gs, en_out
  assign CAUSE = decoder_1_out0 ? {32{1'b0}} : 32'bz;  // Controlled_Buffer controlled_buffer_1
  assign CAUSE = decoder_1_out1 ? 32'h8000000b : 32'bz;  // Controlled_Buffer controlled_buffer_2
  assign CAUSE = decoder_1_out2 ? 32'h4 : 32'bz;  // Controlled_Buffer controlled_buffer_3
  assign CAUSE = decoder_1_out3 ? 32'h6 : 32'bz;  // Controlled_Buffer controlled_buffer_4
  or or_6 (IRQ, EINT, EAL_t, EPL, ILL, RST);
  or or_7 (IRG, RST, d_ff_1_qn);
  or or_8 (CLI, RST, d_ff_2_q);
  assign CAUSE = decoder_1_out4 ? 32'h3 : 32'bz;  // Controlled_Buffer controlled_buffer_5
  assign CAUSE = decoder_1_out5 ? 32'hb : 32'bz;  // Controlled_Buffer controlled_buffer_6
  assign CAUSE = decoder_1_out6 ? {32{1'b0}} : 32'bz;  // Controlled_Buffer controlled_buffer_7
  assign CAUSE = decoder_1_out7 ? 32'h2 : 32'bz;  // Controlled_Buffer controlled_buffer_8

  // Other names for the same wires on the sheet: INT = TRAP

  // Notes on the sheet:
  //   Reset
  //   External Interrupt
  //   Load Address Misaligned
  //   Store Address Misaligned
  //   Environment Break
  //   Environment Call
  //   Instruction Address Misaligned
  //   Illegal Instruction
endmodule

module BinaryToBCD (
  input  [31:0] VIN,
  input  SUP_IN,
  input  SUP_0,
  output [31:0] VOUT,
  output [3:0] DIGIT,
  output SUP_OUT
);

  wire comparator_1_eq, not_1_out;
  wire [31:0] divider_1_rem;

  Divider #(.width(32)) divider_1 (.a(VIN), .b(32'ha), .out(VOUT), .rem(divider_1_rem));  // open: upper
  Comparator #(.width(4)) comparator_1 (.a(divider_1_rem[3:0]), .b(4'b0000), .eq(comparator_1_eq));  // open: gt, lt
  assign DIGIT = not_1_out ? divider_1_rem[3:0] : 4'bz;  // Controlled_Buffer controlled_buffer_1
  not not_1 (not_1_out, SUP_OUT);
  and and_1 (SUP_OUT, comparator_1_eq, SUP_IN, SUP_0);

  // Notes on the sheet:
  //   SUP_IN: pull=up
  //   SUP_0: pull=up
  //   SUP_OUT: pull=up
endmodule
